# Fritzing sketch AboveDiagram (saved by Fritzing 0.9.3b)
breadboards: 1

parts:
  Part8 = Arduino Pro Mini (5V)  # not connected
  Part10 = DeadOn RTC - DS3234 Breakout

nets:
  N1: Part10.SS, Part10.MISO
